# Fritzing sketch FloodDetector (saved by Fritzing 0.9.4)

parts:
  Part1 = Arduino Uno (Rev3)
  Water_Level_Sensor1 = Water Level Sensor
  U1 = ESP8266 WiFi Module [part_number=ESP8266]
  HC-SR04_Sensor_1 = HC-SR04 Ultrasonic Distance Sensor
  Buzzer = Piezo Speaker
  R1 = Resistor [tolerance=±5% resistance=220 package=THT]

nets:
  N1: Part1.D8, Water_Level_Sensor1.SIG
  GND: Part1.GND, U1.GND, HC-SR04_Sensor_1.GND, Buzzer.pin1
  N2: Part1.D0/RX, U1.RX
  N3: Part1.D1/TX, U1.TX
  N4: Part1.D4, HC-SR04_Sensor_1.ECHO
  N5: Part1.D5_PWM, HC-SR04_Sensor_1.TRIG
  N6: Part1.D7, R1.Pin_1
  3V3: Part1.3V3, U1.3.3V
  5V: Part1.5V, HC-SR04_Sensor_1.VCC

custom parts:
  Water Level Sensor: A water level sensor. This sensor operates at 3V to 5V. The Sig (signal) pin outputs an analogue signal that is in proportion to the amount of water in contact with the sensor.
