# Fritzing sketch RelayLamp (saved by Fritzing 0.9.4)
breadboards: 1

parts:
  Part1 = Arduino Uno (Rev3)
  LED1 = LEDs [package=led10mm]
  WeMos_D1_Mini_Relay_Shield_V1 = WeMos D1 Mini Relay Shield V2
  U1 = prefix0000 [chip_label=IC]
  R1 = Photocell (LDR) [package=THT]
  R2 = Resistor [tolerance=±5% resistance=220 package="2512 [SMD]"]

nets:
  N1: Part1.A0, R1.pin_0, R2.Pin_1
  N2: Part1.D7, WeMos_D1_Mini_Relay_Shield_V1.A0
  5V: Part1.5V, WeMos_D1_Mini_Relay_Shield_V1.5V, R1.pin_1
  N3: Part1.GND, WeMos_D1_Mini_Relay_Shield_V1.G, R2.Pin_0
  N4: LED1.A, WeMos_D1_Mini_Relay_Shield_V1.NO
  N5: LED1.C, U1.connector1
  N6: WeMos_D1_Mini_Relay_Shield_V1.COM, U1.connector3

custom parts:
  LEDs: LEDs Standard schematic elements and footprints for 5mm, 3mm, 1206, and 0603 sized LEDs. 5mm - Spark Fun Electronics SKU : COM-00529 (and others)
